// Logisim project Adders.circ as structural Verilog: 4 circuits, main circuit FA0
module FA0 (
  input  a,
  input  b,
  output s,
  output c
);

  wire nor_1_out;

  nor nor_1 (nor_1_out, a, b);
  and and_1 (c, a, b);
  nor nor_2 (s, nor_1_out, c);

  // Notes on the sheet:
  //   14 transistors
  //   FA0
  //   Saffron Liu
  //   2.75
  //   1.75
endmodule

module FA1 (
  input  a,
  input  b,
  output s,
  output c
);

  wire nand_1_out;

  nand nand_1 (nand_1_out, a, b);
  or or_1 (c, a, b);
  nand nand_2 (s, nand_1_out, c);

  // Notes on the sheet:
  //   14 transistors
  //   FA1
  //   Saffron Liu
  //   2.75
  //   1.75
endmodule

module FAopt1 (
  input  A,
  input  B,
  input  Cin,
  output S,
  output Cout
);

  wire nand_1_out, nand_2_out, nor_1_out, nor_2_out, nor_3_out, not_1_out, not_2_out;

  nor nor_1 (nor_1_out, A, B);
  nand nand_1 (nand_1_out, A, B);
  not not_1 (not_1_out, nand_1_out);
  nor nor_2 (nor_2_out, nor_1_out, not_1_out);
  nand nand_2 (nand_2_out, nor_2_out, Cin);
  nor nor_3 (nor_3_out, nor_2_out, Cin);
  not not_2 (not_2_out, nand_2_out);
  nand nand_3 (Cout, nand_1_out, nand_2_out);
  nor nor_4 (S, nor_3_out, not_2_out);

  // Notes on the sheet:
  //   32 transistors
  //   FAopt1
  //   Saffron Liu
  //   If Cin < 2.75: 5.5
  //   If Cin < 2.75: 4.75
  //   If Cin > 2.75: Cin + 2
  //   If Cin > 2.75: Cin + 2.75
endmodule

module FAopt2 (
  input  A,
  input  B,
  input  Cin,
  output S,
  output Cout
);

  wire and_1_out, nand_1_out, nand_2_out, nand_3_out, nor_1_out, nor_2_out, nor_3_out, not_1_out;

  nor nor_1 (nor_1_out, A, B);
  nand nand_1 (nand_1_out, A, B);
  nand nand_2 (nand_2_out, A, Cin);
  nand nand_3 (nand_3_out, B, Cin);
  not not_1 (not_1_out, nand_1_out);
  nand nand_4 (Cout, nand_1_out, nand_2_out, nand_3_out);
  nor nor_2 (nor_2_out, nor_1_out, not_1_out);
  nor nor_3 (nor_3_out, nor_2_out, Cin);
  and and_1 (and_1_out, nor_2_out, Cin);
  nor nor_4 (S, nor_3_out, and_1_out);

  // Notes on the sheet:
  //   42 transistors
  //   Cin + 2.25
  //   FAopt2
  //   Saffron Liu
  //   If Cin < 2.75: 5.5
  //   If Cin > 2.75: Cin + 2.75
endmodule
